// Logisim project control_logic.circ as structural Verilog: 1 circuit, main circuit control_logic
module control_logic (
  input  [31:0] inst,
  input  BrEq,
  input  BrLt,
  output PCSel,
  output RegWEn,
  output [2:0] ImmSel,
  output BrUn,
  output ASel,
  output BSel,
  output [3:0] ALUSel,
  output MemRW,
  output [1:0] WBSel,
  output CSRSel,
  output CSRWen
);

  wire and_1_out, and_2_out, and_3_out, and_4_out, not_1_out, not_2_out, not_3_out, not_5_out, not_7_out,
       not_10_out, not_11_out, not_12_out, not_13_out, not_17_out, not_20_out, not_21_out;

  not not_1 (not_1_out, inst[2]);
  not not_2 (not_2_out, inst[3]);
  not not_3 (not_3_out, inst[4]);
  // NOT_Gate not_4 has open pins: in=inst[5], out=open
  not not_5 (not_5_out, inst[6]);
  // NOT_Gate not_6 has open pins: in=inst[2], out=open
  not not_7 (not_7_out, inst[3]);
  // NOT_Gate not_8 has open pins: in=inst[4], out=open
  // NOT_Gate not_9 has open pins: in=inst[5], out=open
  not not_10 (not_10_out, inst[6]);
  and and_1 (and_1_out, not_1_out, not_2_out, not_3_out, inst[5], not_5_out);
  and and_2 (and_2_out, inst[2], not_7_out, inst[4], not_10_out);
  or or_1 (ImmSel[0], and_1_out, and_2_out);
  not not_11 (not_11_out, inst[2]);
  not not_12 (not_12_out, inst[3]);
  not not_13 (not_13_out, inst[4]);
  // NOT_Gate not_14 has open pins: in=inst[5], out=open
  // NOT_Gate not_15 has open pins: in=inst[6], out=open
  // NOT_Gate not_16 has open pins: in=inst[2], out=open
  not not_17 (not_17_out, inst[3]);
  // NOT_Gate not_18 has open pins: in=inst[4], out=open
  // NOT_Gate not_19 has open pins: in=inst[5], out=open
  not not_20 (not_20_out, inst[6]);
  and and_3 (and_3_out, not_11_out, not_12_out, not_13_out, inst[5], inst[6]);
  and and_4 (and_4_out, inst[2], not_17_out, inst[4], not_20_out);
  or or_2 (ImmSel[1], and_3_out, and_4_out);
  not not_21 (not_21_out, inst[4]);
  and and_5 (ImmSel[2], inst[2], inst[3], not_21_out, inst[5], inst[6]);

  // Other names for the same wires on the sheet: Sel_0 = ImmSel[0]; Sel_1 = ImmSel[1]; Sel_2 = ImmSel[2];
  //   OP_2 = inst[2]; OP_3 = inst[3]; OP_4 = inst[4]; OP_5 = inst[5]; OP_6 = inst[6]

  // Notes on the sheet:
  //   INPUTS to your circuit
  //   DON'T CHANGE THE LOCATIONS OF THE INPUTS AND OUTPUTS!
  //   OUTPUT from your circuit
endmodule
