// Logisim project cpu.circ as structural Verilog: 1 circuit, main circuit cpu
module cpu (
  input  clk,
  input  [31:0] INSTRUCTION,
  input  [31:0] READ_DATA,
  output [31:0] WRITE_ADDRESS,
  output [31:0] PROGRAM_COUNTER,
  output [31:0] ra,
  output [31:0] sp,
  output [31:0] t0,
  output [31:0] t1,
  output [31:0] t2,
  output [31:0] s0,
  output [31:0] s1,
  output [31:0] a0,
  output [31:0] tohost,
  output [3:0] WRITE_ENABLE,
  output [31:0] WRITE_DATA
);

  wire ASel, BrEq, BrLt, BrUn, BSel, csr_1_p2, CSRSel, CSRWen, MemRW, PCSel, RegWEn;
  wire [1:0] WBSel;
  wire [2:0] ImmSel;
  wire [3:0] ALUSel;
  wire [31:0] A, adder_1_out, B, ID_INSTRUCTION, imm, Read_Data_1, Read_Data_2, Result, Write_Data_t;

  Adder #(.width(32)) adder_1 (.a(PROGRAM_COUNTER), .b(32'h4), .out(adder_1_out));  // open: cin, cout
  Register #(.width(32)) PC (.D(adder_1_out), .clk(clk), .Q(PROGRAM_COUNTER));  // open: en, clr
  control_logic control_logic_1 (
    .CSRWen(CSRWen), .PCSel(PCSel), .RegWEn(RegWEn), .ImmSel(ImmSel), .BrUn(BrUn), .ASel(ASel), .BSel(BSel),
    .ALUSel(ALUSel), .MemRW(MemRW), .WBSel(WBSel), .CSRSel(CSRSel), .inst(ID_INSTRUCTION), .BrEq(BrEq),
    .BrLt(BrLt));
  branch_comp branch_comp_1 (.rs1(Read_Data_1), .rs2(Read_Data_2), .BrUn(BrUn), .BrEq(BrEq), .BrLt(BrLt));
  imm_gen imm_gen_1 (.inst(ID_INSTRUCTION), .ImmSel(ImmSel), .imm(imm));
  Register #(.width(32)) register_1 (.D(INSTRUCTION), .clk(clk), .Q(ID_INSTRUCTION));  // open: en, clr
  regfile regfile_1 (
    .rs1(ID_INSTRUCTION[19:15]), .rs2(ID_INSTRUCTION[24:20]), .rd(ID_INSTRUCTION[11:7]),
    .Write_Data(Write_Data_t), .RegWEn(RegWEn), .clk(clk), .ra(ra), .sp(sp), .t0(t0), .t1(t1), .t2(t2),
    .s0(s0), .s1(s1), .a0(a0), .Read_Data_1(Read_Data_1), .Read_Data_2(Read_Data_2));
  Multiplexer #(.enable("false"), .width(32)) multiplexer_1 (
    .in0(Read_Data_1), .in1(PROGRAM_COUNTER), .out(A), .sel(ASel));
  Multiplexer #(.enable("false"), .width(32)) multiplexer_2 (.in0(Read_Data_2), .in1(imm), .out(B), .sel(BSel));
  alu alu_1 (.Result(Result), .A(A), .B(B), .ALUSel(ALUSel));
  // csr csr_1: pin names not known; wires that end beside it: tohost, csr_1_p2

  // Other names for the same wires on the sheet: rd[4:0] = ID_INSTRUCTION[11:7]; rs1[4:0] = ID_INSTRUCTION[19:15];
  //   rs2[4:0] = ID_INSTRUCTION[24:20]

  // Notes on the sheet:
  //   Output to IMEM
  //   IMEM (do **NOT** move this)
  //   Inputs from IMEM
  //   IF
  //   ID
  //   Inputs/Outputs for testing. Do **NOT** move these.
  //   EX
  //   Outputs To DMEM
  //   DMEM (do **NOT** move this)
  //   Inputs From DMEM
endmodule
