// Logisim project imm_gen.circ as structural Verilog: 1 circuit, main circuit imm_gen
module imm_gen (
  input  [31:0] inst,
  input  [2:0] ImmSel,
  output [31:0] imm
);

  wire [31:11] I_imm, S_imm;
  wire [31:12] SB_imm;
  wire [31:20] UJ_imm;

  Multiplexer #(.enable("false"), .select(3), .width(32)) multiplexer_1 (
    .in0({I_imm, inst[30:20]}), .in1({S_imm, inst[30:25], inst[11:7]}),
    .in2({SB_imm, inst[7], inst[30:25], inst[11:8], 1'b0}), .in3({inst[31:12], {12{1'b0}}}),
    .in4({UJ_imm, inst[19:12], inst[20], inst[30:21], 1'b0}), .out(imm), .sel(ImmSel));  // open: in5, in6, in7
  assign I_imm = {{20{inst[31]}}, inst[31]};  // Bit_Extender bit_extender_1
  assign S_imm = {{20{inst[31]}}, inst[31]};  // Bit_Extender bit_extender_2
  assign SB_imm = {{19{inst[31]}}, inst[31]};  // Bit_Extender bit_extender_3
  assign UJ_imm = {{11{inst[31]}}, inst[31]};  // Bit_Extender bit_extender_4

  // Other names for the same wires on the sheet: inst11_8[3:0] = inst[11:8]; S_imm[10:0] = {inst[30:25], inst[11:7]};
  //   SB_imm[11:1] = {inst[7], inst[30:25], inst[11:8]}; U_imm[31:12] = inst[31:12]; I_imm[10:0] = inst[30:20];
  //   inst24_21[3:0] = inst[24:21]; UJ_imm[19:1] = {inst[19:12], inst[20], inst[30:21]}; inst30_25[5:0] = inst[30:25];
  //   inst19_12[7:0] = inst[19:12]

  // Notes on the sheet:
  //   INPUTS to your circuit
  //   DON'T CHANGE THE LOCATIONS OF THE INPUTS AND OUTPUTS!
  //   Assume: I=000; S=001; SB=010; U=011; UJ=100
  //   OUTPUT from your circuit
endmodule
