// Logisim project regfile.circ as structural Verilog: 1 circuit, main circuit regfile
module regfile (
  input  [4:0] rs1,
  input  [4:0] rs2,
  input  [4:0] rd,
  input  [31:0] Write_Data,
  input  RegWEn,
  input  clk,
  input  [31:0] Zero_32,
  output [31:0] ra,
  output [31:0] sp,
  output [31:0] t0,
  output [31:0] t1,
  output [31:0] t2,
  output [31:0] s0,
  output [31:0] s1,
  output [31:0] a0,
  output [31:0] Read_Data_1,
  output [31:0] Read_Data_2
);

  wire write_en_0, write_en_1, write_en_2, write_en_3, write_en_4, write_en_5, write_en_6, write_en_7,
       write_en_8, write_en_9, write_en_10, write_en_11, write_en_12, write_en_13, write_en_14, write_en_15,
       write_en_16, write_en_17, write_en_18, write_en_19, write_en_20, write_en_21, write_en_22,
       write_en_23, write_en_24, write_en_25, write_en_26, write_en_27, write_en_28, write_en_29,
       write_en_30, write_en_31;
  wire [31:0] out0, out3, out4, out11, out12, out13, out14, out15, out16, out17, out18, out19, out20, out21,
       out22, out23, out24, out25, out26, out27, out28, out29, out30, out31;

  Register #(.width(32)) register_1 (.D(Zero_32), .en(write_en_0), .clk(clk), .Q(out0));  // open: clr
  Register #(.width(32)) register_2 (.D(Write_Data), .en(write_en_4), .clk(clk), .Q(out4));  // open: clr
  Register #(.width(32)) register_3 (.D(Write_Data), .en(write_en_8), .clk(clk), .Q(s0));  // open: clr
  Register #(.width(32)) register_4 (.D(Write_Data), .en(write_en_12), .clk(clk), .Q(out12));  // open: clr
  Register #(.width(32)) register_5 (.D(Write_Data), .en(write_en_16), .clk(clk), .Q(out16));  // open: clr
  Register #(.width(32)) register_6 (.D(Write_Data), .en(write_en_20), .clk(clk), .Q(out20));  // open: clr
  Register #(.width(32)) register_7 (.D(Write_Data), .en(write_en_24), .clk(clk), .Q(out24));  // open: clr
  Register #(.width(32)) register_8 (.D(Write_Data), .en(write_en_28), .clk(clk), .Q(out28));  // open: clr
  Register #(.width(32)) register_9 (.D(Write_Data), .en(write_en_1), .clk(clk), .Q(ra));  // open: clr
  Register #(.width(32)) register_10 (.D(Write_Data), .en(write_en_5), .clk(clk), .Q(t0));  // open: clr
  Register #(.width(32)) register_11 (.D(Write_Data), .en(write_en_9), .clk(clk), .Q(s1));  // open: clr
  Register #(.width(32)) register_12 (.D(Write_Data), .en(write_en_13), .clk(clk), .Q(out13));  // open: clr
  Register #(.width(32)) register_13 (.D(Write_Data), .en(write_en_17), .clk(clk), .Q(out17));  // open: clr
  Register #(.width(32)) register_14 (.D(Write_Data), .en(write_en_21), .clk(clk), .Q(out21));  // open: clr
  Register #(.width(32)) register_15 (.D(Write_Data), .en(write_en_25), .clk(clk), .Q(out25));  // open: clr
  Register #(.width(32)) register_16 (.D(Write_Data), .en(write_en_29), .clk(clk), .Q(out29));  // open: clr
  Register #(.width(32)) register_17 (.D(Write_Data), .en(write_en_2), .clk(clk), .Q(sp));  // open: clr
  Register #(.width(32)) register_18 (.D(Write_Data), .en(write_en_6), .clk(clk), .Q(t1));  // open: clr
  Register #(.width(32)) register_19 (.D(Write_Data), .en(write_en_10), .clk(clk), .Q(a0));  // open: clr
  Register #(.width(32)) register_20 (.D(Write_Data), .en(write_en_14), .clk(clk), .Q(out14));  // open: clr
  Register #(.width(32)) register_21 (.D(Write_Data), .en(write_en_18), .clk(clk), .Q(out18));  // open: clr
  Register #(.width(32)) register_22 (.D(Write_Data), .en(write_en_22), .clk(clk), .Q(out22));  // open: clr
  Register #(.width(32)) register_23 (.D(Write_Data), .en(write_en_26), .clk(clk), .Q(out26));  // open: clr
  Register #(.width(32)) register_24 (.D(Write_Data), .en(write_en_30), .clk(clk), .Q(out30));  // open: clr
  Register #(.width(32)) register_25 (.D(Write_Data), .en(write_en_3), .clk(clk), .Q(out3));  // open: clr
  Register #(.width(32)) register_26 (.D(Write_Data), .en(write_en_7), .clk(clk), .Q(t2));  // open: clr
  Register #(.width(32)) register_27 (.D(Write_Data), .en(write_en_11), .clk(clk), .Q(out11));  // open: clr
  Register #(.width(32)) register_28 (.D(Write_Data), .en(write_en_15), .clk(clk), .Q(out15));  // open: clr
  Register #(.width(32)) register_29 (.D(Write_Data), .en(write_en_19), .clk(clk), .Q(out19));  // open: clr
  Register #(.width(32)) register_30 (.D(Write_Data), .en(write_en_23), .clk(clk), .Q(out23));  // open: clr
  Register #(.width(32)) register_31 (.D(Write_Data), .en(write_en_27), .clk(clk), .Q(out27));  // open: clr
  Register #(.width(32)) register_32 (.D(Write_Data), .en(write_en_31), .clk(clk), .Q(out31));  // open: clr
  Demultiplexer #(.enable("false"), .select(5)) demultiplexer_1 (
    .out0(write_en_0), .out1(write_en_1), .out2(write_en_2), .out3(write_en_3), .out4(write_en_4),
    .out5(write_en_5), .out6(write_en_6), .out7(write_en_7), .out8(write_en_8), .out9(write_en_9),
    .out10(write_en_10), .out11(write_en_11), .out12(write_en_12), .out13(write_en_13), .out14(write_en_14),
    .out15(write_en_15), .out16(write_en_16), .out17(write_en_17), .out18(write_en_18), .out19(write_en_19),
    .out20(write_en_20), .out21(write_en_21), .out22(write_en_22), .out23(write_en_23), .out24(write_en_24),
    .out25(write_en_25), .out26(write_en_26), .out27(write_en_27), .out28(write_en_28), .out29(write_en_29),
    .out30(write_en_30), .out31(write_en_31), .in(RegWEn), .sel(rd));
  Multiplexer #(.enable("false"), .select(5), .width(32)) multiplexer_1 (
    .in0(out0), .in1(ra), .in2(sp), .in3(out3), .in4(out4), .in5(t0), .in6(t1), .in7(t2), .in8(s0), .in9(s1),
    .in10(a0), .in11(out11), .in12(out12), .in13(out13), .in14(out14), .in15(out15), .in16(out16),
    .in17(out17), .in18(out18), .in19(out19), .in20(out20), .in21(out21), .in22(out22), .in23(out23),
    .in24(out24), .in25(out25), .in26(out26), .in27(out27), .in28(out28), .in29(out29), .in30(out30),
    .in31(out31), .out(Read_Data_1), .sel(rs1));
  Multiplexer #(.enable("false"), .select(5), .width(32)) multiplexer_2 (
    .in0(out0), .in1(ra), .in2(sp), .in3(out3), .in4(out4), .in5(t0), .in6(t1), .in7(t2), .in8(s0), .in9(s1),
    .in10(a0), .in11(out11), .in12(out12), .in13(out13), .in14(out14), .in15(out15), .in16(out16),
    .in17(out17), .in18(out18), .in19(out19), .in20(out20), .in21(out21), .in22(out22), .in23(out23),
    .in24(out24), .in25(out25), .in26(out26), .in27(out27), .in28(out28), .in29(out29), .in30(out30),
    .in31(out31), .out(Read_Data_2), .sel(rs2));

  // Other names for the same wires on the sheet: out1[31:0] = ra; out2[31:0] = sp; out5[31:0] = t0; out6[31:0] = t1;
  //   out7[31:0] = t2; out8[31:0] = s0; out9[31:0] = s1; out10[31:0] = a0; read_data1[31:0] = Read_Data_1;
  //   read_data2[31:0] = Read_Data_2; read_reg1[4:0] = rs1; read_reg2[4:0] = rs2; write_en = RegWEn;
  //   write_reg[4:0] = rd

  // Notes on the sheet:
  //   INPUTS to your circuit
  //   DON'T CHANGE THE LOCATIONS OF THE INPUTS AND OUTPUTS!
  //   These are DEBUG/TEST outputs from your circuit.
  //   OUTPUTS from your circuit
endmodule
